# Fritzing sketch motor_door (saved by Fritzing 0.9.1b)
breadboards: 1

parts:
  MCU = Arduino Uno (Rev3)
  LED1 = LED - 5mm [color="Red (633nm)" package="5 mm [THT]"]
  S1_/_Magnetic_sensor = Pushbutton [package=THT]
  R3 = Resistor [tolerance=±5% resistance=330 package=THT]
  J2_/_i2c = female pin header, 2 pins [form="♀ (female)"]
  S2_/_Magnetic_sensor = Pushbutton [package=THT]
  R4 = Resistor [tolerance=±5% resistance=330 package=THT]
  R1 = Resistor [tolerance=±20% resistance=10k package=THT]
  R2 = Resistor [tolerance=±20% resistance=10k package=THT]
  LED2 = LED - 5mm [color="Red (633nm)" package="5 mm [THT]"]
  IC1 = L293D [package=THT]
  M1 = DC Motor
  J1_/_Lock_servo = Basic Servo

nets:
  N1: MCU.A0, S2_/_Magnetic_sensor.leg1, R2.Pin_0
  N2: MCU.A1, S1_/_Magnetic_sensor.leg1, R1.Pin_0
  N3: MCU.A4/SDA, J2_/_i2c.pin2
  N4: MCU.D9_PWM, J1_/_Lock_servo.pulse
  N5: MCU.D11_PWM/MOSI, IC1.Enable_1
  GND: MCU.GND, R3.Pin_0, R4.Pin_0, IC1.0V, J1_/_Lock_servo.gnd
  N6: MCU.A5/SCL, J2_/_i2c.pin1
  N7: MCU.D3_PWM, IC1.In_1
  N8: MCU.D4, IC1.In_2
  5V: MCU.5V, R1.Pin_1, R2.Pin_1, J1_/_Lock_servo.vcc
  N9: LED1.cathode, R3.Pin_1
  N10: LED1.anode, S1_/_Magnetic_sensor.leg0
  N11: S2_/_Magnetic_sensor.leg0, LED2.anode
  N12: R4.Pin_1, LED2.cathode
  N13: IC1.Out_1_(_Controlled_by_Enable_1_), M1.pin_2
  N14: IC1.Out_2_(_Controlled_by_Enable_1_), M1.pin_1
  9V: IC1.+Vmotor

notes:
  Motor door / i2c device
