# Fritzing sketch sensing-device (saved by Fritzing 0.9.1b)
breadboards: 1

parts:
  MCU = Arduino Uno (Rev3)
  DHT22 = DHT22 Humidity and Temperature Sensor
  R1 = Resistor [tolerance=±5% resistance=10k package=THT]
  J1_/_i2c = female pin header, 2 pins [form="♀ (female)"]

nets:
  N1: MCU.A4/SDA, J1_/_i2c.pin2
  GND: MCU.GND, DHT22.GND
  N2: MCU.A5/SCL, J1_/_i2c.pin1
  N3: MCU.D4, DHT22.DATA, R1.Pin_1
  5V: MCU.5V, DHT22.VDD, R1.Pin_0

notes:
  DHT22 sensing device / i2c device
