# Fritzing sketch servo_door (saved by Fritzing 0.9.1b)
breadboards: 1

parts:
  MCU = Arduino Uno (Rev3)
  LED1 = LED - 5mm [color="Red (633nm)" package="5 mm [THT]"]
  S1_/_Magnetic_sensor = Pushbutton [package=THT]
  R1 = Resistor [tolerance=±20% resistance=10k package=THT]
  R2 = Resistor [tolerance=±5% resistance=330 package=THT]
  J1_/_Door_servo = Basic Servo
  J2_/_Lock_servo = Basic Servo
  J3_/_i2c = female pin header, 2 pins [form="♀ (female)"]

nets:
  N1: MCU.A4/SDA, J3_/_i2c.pin2
  N2: MCU.D9_PWM, J2_/_Lock_servo.pulse
  N3: MCU.D10_PWM/SS, J1_/_Door_servo.pulse
  GND: MCU.GND, R1.Pin_0, R2.Pin_0, J1_/_Door_servo.gnd, J2_/_Lock_servo.gnd
  N4: MCU.A5/SCL, J3_/_i2c.pin1
  N5: MCU.D4, LED1.anode, S1_/_Magnetic_sensor.leg0, R1.Pin_1
  5V: MCU.5V, S1_/_Magnetic_sensor.leg1, J1_/_Door_servo.vcc, J2_/_Lock_servo.vcc
  N6: LED1.cathode, R2.Pin_1

notes:
  Servo door / i2c device
