# Fritzing sketch waterdispenser (saved by Fritzing 0.9.1b)
breadboards: 1

parts:
  MCU = Arduino Uno (Rev3)
  R1 = Resistor [tolerance=±5% resistance=10k package=THT]  # not connected
  J1_/_i2c = female pin header, 2 pins [form="♀ (female)"]
  VALVE = Plastic Solenoid Valve
  Relay = RELAY-SOLIDSTATE [package=relay-s108t02]
  Soil_moisture_sensor = Analog Sensor
  R2 = Resistor [tolerance=±5% resistance=10k package=THT]

nets:
  N1: MCU.A2, Soil_moisture_sensor.+, R2.Pin_1
  N2: MCU.A4/SDA, J1_/_i2c.pin2
  GND: MCU.GND, VALVE.connector1, Relay.T2, Relay.-, Soil_moisture_sensor.-
  N3: MCU.A5/SCL, J1_/_i2c.pin1
  N4: MCU.D2, Relay.+
  5V: MCU.5V, R2.Pin_0
  12V: VALVE.connector2, Relay.T1

notes:
  Water dispenser / i2c device
