# Fritzing sketch window (saved by Fritzing 0.9.1b)
breadboards: 1

parts:
  MCU = Arduino Uno (Rev3)
  LED1 = LED - 5mm [color="Red (633nm)" package="5 mm [THT]"]
  S1_/_Magnetic_sensor = Pushbutton [package=THT]
  R1 = Resistor [tolerance=±20% resistance=10k package=THT]
  R2 = Resistor [tolerance=±5% resistance=330 package=THT]
  J1_/_Left_window = Basic Servo
  J2_/_Right_window = Basic Servo
  J3_/_Window_lock = Basic Servo
  J4_/_i2c = female pin header, 2 pins [form="♀ (female)"]

nets:
  N1: MCU.A4/SDA, J4_/_i2c.pin2
  N2: MCU.D8, J3_/_Window_lock.pulse
  N3: MCU.D9_PWM, J2_/_Right_window.pulse
  N4: MCU.D10_PWM/SS, J1_/_Left_window.pulse
  GND: MCU.GND, R1.Pin_0, R2.Pin_0, J1_/_Left_window.gnd, J2_/_Right_window.gnd, J3_/_Window_lock.gnd
  N5: MCU.A5/SCL, J4_/_i2c.pin1
  N6: MCU.D4, LED1.anode, S1_/_Magnetic_sensor.leg0, R1.Pin_1
  5V: MCU.5V, S1_/_Magnetic_sensor.leg1, J1_/_Left_window.vcc, J2_/_Right_window.vcc, J3_/_Window_lock.vcc
  N7: LED1.cathode, R2.Pin_1

notes:
  Window / i2c device
